// Logisim project cpu.circ as structural Verilog: 4 circuits, main circuit main
module main (
  input  [1:0] OperandB,
  input  [1:0] StoreOp,
  input  [1:0] OperandA,
  input  [7:0] ImmOp,
  input  CLK,
  input  Subtract,
  input  BitNAND
);

  wire decoder_1_out0, decoder_1_out1, decoder_1_out2, decoder_1_out3, decoder_2_out0, decoder_2_out1,
       decoder_2_out2, decoder_2_out3, decoder_3_out0, decoder_3_out1, decoder_3_out2;
  wire [7:0] alu_1_result, controlled_buffer_1_out, controlled_buffer_2_out, RegA_q, RegB_q, RegC_q;

  ROM #(.addrWidth(16)) rom_1 ();  // open: addr, data
  Register RegA (.D(alu_1_result), .en(decoder_3_out0), .clk(CLK), .Q(RegA_q));  // open: clr
  assign controlled_buffer_1_out = decoder_1_out0 ? RegA_q : 8'bz;  // Controlled_Buffer controlled_buffer_1
  assign controlled_buffer_2_out = decoder_2_out0 ? RegA_q : 8'bz;  // Controlled_Buffer controlled_buffer_2
  Decoder #(.select(2)) decoder_1 (
    .out0(decoder_1_out0), .out1(decoder_1_out1), .out2(decoder_1_out2), .out3(decoder_1_out3), .sel(OperandA));  // open: en
  Register RegB (.D(alu_1_result), .en(decoder_3_out1), .clk(CLK), .Q(RegB_q));  // open: clr
  assign controlled_buffer_1_out = decoder_1_out1 ? RegB_q : 8'bz;  // Controlled_Buffer controlled_buffer_3
  assign controlled_buffer_2_out = decoder_2_out1 ? RegB_q : 8'bz;  // Controlled_Buffer controlled_buffer_4
  Register RegC (.D(alu_1_result), .en(decoder_3_out2), .clk(CLK), .Q(RegC_q));  // open: clr
  Decoder #(.select(2)) decoder_2 (
    .out0(decoder_2_out0), .out1(decoder_2_out1), .out2(decoder_2_out2), .out3(decoder_2_out3), .sel(OperandB));  // open: en
  assign controlled_buffer_1_out = decoder_1_out2 ? RegC_q : 8'bz;  // Controlled_Buffer controlled_buffer_5
  assign controlled_buffer_2_out = decoder_2_out2 ? RegC_q : 8'bz;  // Controlled_Buffer controlled_buffer_6
  RAM #(.addrWidth(16)) ram_1 ();  // open: addr, we, oe, clk, din, dout
  Decoder #(.select(2)) decoder_3 (
    .out0(decoder_3_out0), .out1(decoder_3_out1), .out2(decoder_3_out2), .sel(StoreOp));  // open: out3, en
  assign controlled_buffer_1_out = decoder_1_out3 ? ImmOp : 8'bz;  // Controlled_Buffer controlled_buffer_7
  assign controlled_buffer_2_out = decoder_2_out3 ? ImmOp : 8'bz;  // Controlled_Buffer controlled_buffer_8
  ALU alu_1 (
    .A(controlled_buffer_1_out), .B(controlled_buffer_2_out), .Subtract(Subtract), .BitNAND(BitNAND),
    .Result(alu_1_result));
endmodule

module ALU (
  input  [7:0] A,
  input  [7:0] B,
  input  Subtract,
  input  BitNAND,
  output [7:0] Result
);

  wire [7:0] adder_1_out, nand_1_out, xor_1_out;

  xor xor_1 (xor_1_out[0], B[0], Subtract);
  xor xor_2 (xor_1_out[1], B[1], Subtract);
  xor xor_3 (xor_1_out[2], B[2], Subtract);
  xor xor_4 (xor_1_out[3], B[3], Subtract);
  nand nand_1 (nand_1_out[0], A[0], B[0]);
  nand nand_2 (nand_1_out[1], A[1], B[1]);
  nand nand_3 (nand_1_out[2], A[2], B[2]);
  nand nand_4 (nand_1_out[3], A[3], B[3]);
  xor xor_5 (xor_1_out[4], B[4], Subtract);
  xor xor_6 (xor_1_out[5], B[5], Subtract);
  xor xor_7 (xor_1_out[6], B[6], Subtract);
  xor xor_8 (xor_1_out[7], B[7], Subtract);
  nand nand_5 (nand_1_out[4], A[4], B[4]);
  nand nand_6 (nand_1_out[5], A[5], B[5]);
  nand nand_7 (nand_1_out[6], A[6], B[6]);
  nand nand_8 (nand_1_out[7], A[7], B[7]);
  Adder adder_1 (.a(A), .b(xor_1_out), .out(adder_1_out), .cin(Subtract));  // open: cout
  Multiplexer #(.width(8)) multiplexer_1 (.in0(adder_1_out), .in1(nand_1_out), .out(Result), .sel(BitNAND));
endmodule

module JKOverwrite (
  input  D,
  input  Overwrite,
  input  CLK,
  output Q
);

  wire nand_1_out, nand_2_out, nand_3_out, nand_4_out, not_1_out, or_1_out;

  not not_1 (not_1_out, D);
  nand nand_1 (nand_1_out, D, Overwrite);
  nand nand_2 (nand_2_out, not_1_out, Overwrite);
  J_K_Flip_Flop j_k_ff_1 (.J(nand_3_out), .K(nand_4_out), .clk(or_1_out), .Q(Q));  // open: Qn, preset, reset
  nand nand_3 (nand_3_out, nand_1_out, Overwrite);
  nand nand_4 (nand_4_out, nand_2_out, Overwrite);
  or or_1 (or_1_out, Overwrite, CLK);
endmodule

module PC (
  input  [15:0] Addr,
  input  Overwrite,
  input  CLK,
  output [15:0] Q
);

  wire not_1_out, not_2_out, not_3_out, not_4_out, not_5_out, not_6_out, not_7_out, not_8_out, not_9_out,
       not_10_out, not_11_out, not_12_out, not_13_out, not_14_out, not_15_out, not_16_out, undriven;

  not not_1 (not_1_out, CLK);
  not not_2 (not_2_out, Q[7]);
  JKOverwrite jkoverwrite_1 (.D(Addr[0]), .Overwrite(Overwrite), .CLK(not_1_out), .Q(Q[0]));
  not not_3 (not_3_out, Q[0]);
  JKOverwrite jkoverwrite_2 (.D(Addr[8]), .Overwrite(Overwrite), .CLK(not_2_out), .Q(Q[8]));
  not not_4 (not_4_out, Q[8]);
  JKOverwrite jkoverwrite_3 (.D(Addr[1]), .Overwrite(Overwrite), .CLK(not_3_out), .Q(Q[1]));
  JKOverwrite jkoverwrite_4 (.D(Addr[9]), .Overwrite(undriven), .CLK(not_4_out), .Q(Q[9]));
  not not_5 (not_5_out, Q[1]);
  not not_6 (not_6_out, Q[9]);
  JKOverwrite jkoverwrite_5 (.D(Addr[2]), .Overwrite(Overwrite), .CLK(not_5_out), .Q(Q[2]));
  JKOverwrite jkoverwrite_6 (.D(Addr[10]), .Overwrite(Overwrite), .CLK(not_6_out), .Q(Q[10]));
  not not_7 (not_7_out, Q[2]);
  not not_8 (not_8_out, Q[10]);
  JKOverwrite jkoverwrite_7 (.D(Addr[3]), .Overwrite(Overwrite), .CLK(not_7_out), .Q(Q[3]));
  not not_9 (not_9_out, Q[3]);
  JKOverwrite jkoverwrite_8 (.D(Addr[11]), .Overwrite(Overwrite), .CLK(not_8_out), .Q(Q[11]));
  not not_10 (not_10_out, Q[11]);
  JKOverwrite jkoverwrite_9 (.D(Addr[4]), .Overwrite(Overwrite), .CLK(not_9_out), .Q(Q[4]));
  not not_11 (not_11_out, Q[4]);
  JKOverwrite jkoverwrite_10 (.D(Addr[12]), .Overwrite(Overwrite), .CLK(not_10_out), .Q(Q[12]));
  not not_12 (not_12_out, Q[12]);
  JKOverwrite jkoverwrite_11 (.D(Addr[5]), .Overwrite(Overwrite), .CLK(not_11_out), .Q(Q[5]));
  JKOverwrite jkoverwrite_12 (.D(Addr[13]), .Overwrite(Overwrite), .CLK(not_12_out), .Q(Q[13]));
  not not_13 (not_13_out, Q[5]);
  not not_14 (not_14_out, Q[13]);
  JKOverwrite jkoverwrite_13 (.D(Addr[6]), .Overwrite(Overwrite), .CLK(not_13_out), .Q(Q[6]));
  not not_15 (not_15_out, Q[6]);
  JKOverwrite jkoverwrite_14 (.D(Addr[14]), .Overwrite(Overwrite), .CLK(not_14_out), .Q(Q[14]));
  not not_16 (not_16_out, Q[14]);
  JKOverwrite jkoverwrite_15 (.D(Addr[7]), .Overwrite(Overwrite), .CLK(not_15_out), .Q(Q[7]));
  JKOverwrite jkoverwrite_16 (.D(Addr[15]), .Overwrite(Overwrite), .CLK(not_16_out), .Q(Q[15]));
endmodule
